// Logisim project 29_lecture.pptx.circ as structural Verilog: 1 circuit, main circuit main
module main (
  input  Positive_1,
  input  Negative_1,
  input  Postivie_2,
  input  Neagtive_2,
  input  Positive_3,
  input  Neagtive_3,
  input  [1:0] in_7
);

  wire clock_1_out, clock_2_out, clock_3_out, decoder_1_out1, decoder_1_out2, decoder_1_out3,
       multiplexer_1_out, multiplexer_2_out, nand_1_out, nand_2_out, nand_3_out, nand_4_out, nand_5_out,
       nand_6_out, nand_7_out, nand_8_out, nand_9_out, nand_10_out, nand_11_out, nand_12_out, nand_13_out,
       nand_14_out, nand_15_out, nand_16_out, nand_17_out, nand_18_out;

  Clock clock_1 (.out(clock_1_out));
  Clock clock_2 (.out(clock_2_out));
  Clock clock_3 (.out(clock_3_out));
  nand nand_1 (nand_1_out, Positive_1, clock_1_out);
  nand nand_2 (nand_2_out, clock_1_out, Negative_1);
  nand nand_3 (nand_3_out, Postivie_2, clock_2_out);
  nand nand_4 (nand_4_out, clock_2_out, Neagtive_2);
  nand nand_5 (nand_5_out, Positive_3, clock_3_out);
  nand nand_6 (nand_6_out, clock_3_out, Neagtive_3);
  Multiplexer #(.select(2), .enable("false")) multiplexer_1 (
    .in1(nand_1_out), .in2(nand_3_out), .in3(nand_5_out), .out(multiplexer_1_out), .sel(in_7));  // open: in0
  Multiplexer #(.select(2), .enable("false")) multiplexer_2 (
    .in1(nand_2_out), .in2(nand_4_out), .in3(nand_6_out), .out(multiplexer_2_out), .sel(in_7));  // open: in0
  nand nand_7 (nand_7_out, nand_8_out, nand_8_out);
  nand nand_8 (nand_8_out, decoder_1_out1, multiplexer_1_out);
  Decoder #(.select(2), .enable("false")) decoder_1 (
    .out1(decoder_1_out1), .out2(decoder_1_out2), .out3(decoder_1_out3), .sel(in_7));  // open: out0
  nand nand_9 (nand_9_out, nand_11_out, nand_11_out);
  nand nand_10 (nand_10_out, nand_12_out, nand_12_out);
  nand nand_11 (nand_11_out, decoder_1_out3, multiplexer_1_out);
  nand nand_12 (nand_12_out, decoder_1_out2, multiplexer_1_out);
  nand nand_13 (nand_13_out, nand_15_out, nand_15_out);
  nand nand_14 (nand_14_out, nand_16_out, nand_16_out);
  nand nand_15 (nand_15_out, decoder_1_out2, multiplexer_2_out);
  nand nand_16 (nand_16_out, decoder_1_out1, multiplexer_2_out);
  nand nand_17 (nand_17_out, nand_18_out, nand_18_out);
  nand nand_18 (nand_18_out, decoder_1_out3, multiplexer_2_out);

  // Notes on the sheet:
  //   PWM 1
  //   PWM 2
  //   PWM 3
endmodule
